# Fritzing sketch OSchlemmer (saved by Fritzing 0.9.2b)
breadboards: 1

parts:
  Bauteil1 = Arduino Uno (Rev3)
  S1 = Pushbutton [package="[THT]"]
  R1 = Resistor [tolerance=±5% resistance=10k package=THT]
  R2 = Rotary Potentiometer (Small) [maximum_resistance=47kΩ package=THT]
  Status = LED - 5mm [color="Red (633nm)" package="5 mm [THT]"]
  R3 = Resistor [tolerance=±5% resistance=100 package=THT]
  Fakel = LED - 5mm [color="Yellow (585nm)" package="5 mm [THT]"]
  R4 = Resistor [tolerance=±5% resistance=100 package=THT]
  Servo1 = Basic Servo
  Servo2 = Basic Servo
  Servo3 = Basic Servo
  Servo4 = Basic Servo

nets:
  N1: Bauteil1.A0, S1.Pin_3, S1.Pin_4, R1.Pin_1
  N2: Bauteil1.A2, R2.wiper
  N3: Bauteil1.D10_PWM/SS, Fakel.anode
  N4: Bauteil1.D11_PWM/MOSI, Status.anode
  GND: Bauteil1.GND, R1.Pin_0, R2.leg1, R3.Pin_0, R4.Pin_0
  N5: Bauteil1.D2, Servo1.pulse
  N6: Bauteil1.D3_PWM, Servo2.pulse
  N7: Bauteil1.D4, Servo3.pulse
  N8: Bauteil1.D5_PWM, Servo4.pulse
  5V: Bauteil1.5V, Bauteil1.VIN, S1.Pin_1, S1.Pin_2, R2.leg2
  N9: Status.cathode, R3.Pin_1
  N10: Fakel.cathode, R4.Pin_1
