# Fritzing sketch RemoteAdjustableDesk (saved by Fritzing 0.9.5d)
breadboards: 1

parts:
  R1 = Resistor [tolerance=±5% resistance=10k package=THT]
  S1 = Pushbutton [package="[THT]"]
  R2 = Resistor [tolerance=±5% resistance=10k package=THT]
  S2 = Pushbutton [package="[THT]"]
  Arduino_Ethernet = Arduino Uno (Rev3)
  R3 = Resistor [tolerance=±5% resistance=100 package=THT]
  LED1 = LED - 5mm [color="Red (633nm)" package="5 mm [THT]"]
  R4 = Resistor [tolerance=±5% resistance=100 package=THT]
  LED2 = LED - 5mm [color="Red (633nm)" package="5 mm [THT]"]
  J1 = Basic Servo
  J2 = Basic Servo
  C1 = Electrolytic Capacitor [capacitance=4.7mF voltage=10V package="100 mil [THT, electrolytic]"]
  R5 = Rotary Potentiometer (Small) [maximum_resistance=47kΩ package=THT]

nets:
  VCC: R1.Pin_0, R2.Pin_0, Arduino_Ethernet.5V, J1.vcc, J2.vcc, C1.+, R5.leg2
  N1: R1.Pin_1, S1.Pin_3, S1.Pin_4, Arduino_Ethernet.A4/SDA
  GND: S1.Pin_1, S1.Pin_2, S2.Pin_1, S2.Pin_2, Arduino_Ethernet.GND, R3.Pin_1, R4.Pin_1, J1.gnd, J2.gnd, C1.-, R5.leg1
  N2: R2.Pin_1, S2.Pin_3, S2.Pin_4, Arduino_Ethernet.A5/SCL
  N3: Arduino_Ethernet.A0, R5.wiper
  N4: Arduino_Ethernet.A2, J2.pulse
  N5: Arduino_Ethernet.A3, J1.pulse
  N6: Arduino_Ethernet.D5_PWM, LED1.anode
  N7: Arduino_Ethernet.D6_PWM, LED2.anode
  N8: R3.Pin_0, LED1.cathode
  N9: R4.Pin_0, LED2.cathode
